# Fritzing sketch 2 Bat 2 Esc 2 N20 1 BLess 1 Rec (saved by Fritzing 0.9.3b)

parts:
  Mod1 = flyskyr6b
  U2 = LIPO-110mAh [package=lipo-110]
  U3 = LIPO-110mAh [package=lipo-110]
  920KV_Motor1 = DJI 920 KV Motor
  J1 = screw terminal, 3 pins
  J2 = screw terminal, 4 pins
  J3 = screw terminal, 3 pins
  J4 = screw terminal, 4 pins
  A6 = ESC 1A 5V
  A7 = ESC 1A 5V
  Componente1 = Pololu 3.3V Step-Up Voltage Regulator U1V11F3
  Componente2 = Pololu 3.3V Step-Up Voltage Regulator U1V11F3
  A8 = Littlebee 20A ESC

nets:
  N1: Mod1.CH4, A8.Pin_7
  N2: Mod1.CH5, Mod1.CH6, A6.Pin_1, A7.Pin_1
  N3: Mod1.connector14, Mod1.GND, A8.Pin_6
  N4: U2.+, J1.pin1
  N5: U2.-, J3.pin3
  N6: U3.+, J1.pin2
  N7: U3.-, J3.pin2
  N8: 920KV_Motor1.w, A8.Pin_3
  N9: 920KV_Motor1.v, A8.Pin_4
  N10: 920KV_Motor1.u, A8.Pin_5
  N11: J1.pin3, J2.pin1
  N12: J2.pin2, A6.Pin_4
  N13: J2.pin3, A7.Pin_4
  N14: J2.pin4, A8.Pin_2
  N15: J3.pin1, J4.pin4
  N16: J4.pin1, A8.Pin_1
  N17: J4.pin2, A7.Pin_5
  N18: J4.pin3, A6.Pin_5
  N19: A6.Pin_2, Componente1.IN2
  N20: A6.Pin_3, Componente1.IN1
  N21: A7.Pin_2, Componente2.IN2
  N22: A7.Pin_3, Componente2.IN1

custom parts:
  flyskyr6b: flysky r6b 6ch rc receiver module. Pcb view is 3*7 header pins, 3 female headers will let the board plug in to the receiver, or connect via wires as you choose.
  DJI 920 KV Motor: DJI Brushless Outrunner 2212/920K Motor F330-550
  ESC 1A 5V: ESC 1A 5V.
  Littlebee 20A ESC: LittleBee 20A 2-4 LiPo Battery OPTO ESC Brushless Speed Controller for RC FPV Multicopter.
