# Fritzing sketch Combot (saved by Fritzing 0.9.10b)
breadboards: 1

parts:
  Mod1 = flyskyr6b  # not connected
  U2 = LIPO-110mAh [package=lipo-110]
  U3 = LIPO-110mAh [package=lipo-110]
  Componente1 = ESC MLF1218
  920KV_Motor1 = DJI 920 KV Motor
  M1 = DC Motor [voltage_(max)=6V voltage_(min)=3V]  # not connected
  M2 = DC Motor [voltage_(max)=6V voltage_(min)=3V]  # not connected

nets:
  N1: U2.+, U3.+, Componente1.V+
  N2: U2.-, U3.-, Componente1.GND, Componente1.GND*, 920KV_Motor1.w
  N3: Componente1.PPM, 920KV_Motor1.v
  N4: Componente1.+5, 920KV_Motor1.u

custom parts:
  flyskyr6b: flysky r6b 6ch rc receiver module. Pcb view is 3*7 header pins, 3 female headers will let the board plug in to the receiver, or connect via wires as you choose.
  ESC MLF1218: ESC (Electronic Speed Control) for Cheerson CX-20 quadcopter
  DJI 920 KV Motor: DJI Brushless Outrunner 2212/920K Motor F330-550
