# Fritzing sketch Fork (saved by Fritzing 0.9.10b)

parts:
  Mod1 = flyskyr6b
  U2 = LIPO-110mAh [package=lipo-110]
  U3 = LIPO-110mAh [package=lipo-110]
  920KV_Motor1 = DJI 920 KV Motor
  M3 = DC Motor [voltage_(max)=6V voltage_(min)=3V]
  A2 = Littlebee 20A ESC
  A3 = Littlebee 20A ESC
  J1 = screw terminal, 3 pins
  J2 = screw terminal, 4 pins
  J3 = screw terminal, 3 pins
  J4 = screw terminal, 4 pins
  A4 = Littlebee 20A ESC
  M4 = DC Motor [voltage_(max)=6V voltage_(min)=3V]

nets:
  N1: Mod1.CH1, Mod1.CH2, A3.Pin_7
  N2: Mod1.CH3, Mod1.CH4, A4.Pin_7
  N3: Mod1.CH5, Mod1.CH6, A2.Pin_7
  N4: Mod1.connector14, Mod1.GND, A2.Pin_6, A3.Pin_6, A4.Pin_6
  N5: U2.+, J1.pin1
  N6: U2.-, J3.pin3
  N7: U3.+, J1.pin2
  N8: U3.-, J3.pin2
  N9: 920KV_Motor1.w, A3.Pin_3
  N10: 920KV_Motor1.v, A3.Pin_4
  N11: 920KV_Motor1.u, A3.Pin_5
  N12: M3.pin_1, A2.Pin_5
  N13: M3.pin_2, A2.Pin_3
  N14: A2.Pin_1, J2.pin2
  N15: A2.Pin_2, J4.pin3
  N16: A3.Pin_1, J2.pin4
  N17: A3.Pin_2, J4.pin1
  N18: J1.pin3, J2.pin1
  N19: J2.pin3, A4.Pin_1
  N20: J3.pin1, J4.pin4
  N21: J4.pin2, A4.Pin_2
  N22: A4.Pin_3, M4.pin_2
  N23: A4.Pin_5, M4.pin_1

custom parts:
  flyskyr6b: flysky r6b 6ch rc receiver module. Pcb view is 3*7 header pins, 3 female headers will let the board plug in to the receiver, or connect via wires as you choose.
  DJI 920 KV Motor: DJI Brushless Outrunner 2212/920K Motor F330-550
  Littlebee 20A ESC: LittleBee 20A 2-4 LiPo Battery OPTO ESC Brushless Speed Controller for RC FPV Multicopter.
